# Fritzing sketch FullColorLED回路図 (saved by Fritzing 0.9.2b)
breadboards: 1

parts:
  arduino = Arduino Uno (Rev3)
  R1 = Resistor [tolerance=±5% resistance=330 package=THT]
  R2 = Resistor [tolerance=±5% resistance=220 package=THT]
  R3 = Resistor [tolerance=±5% resistance=220 package=THT]
  LED1 = RGB LED (com. cathode, rbg) [package="5 mm [THT]"]

nets:
  N1: arduino.D9_PWM, R1.Pin_1
  N2: arduino.D10_PWM/SS, R2.Pin_1
  N3: arduino.D11_PWM/MOSI, R3.Pin_1
  N4: arduino.GND, LED1.common_cathode
  N5: R1.Pin_0, LED1.red_anode
  N6: R2.Pin_0, LED1.blue_anode
  N7: R3.Pin_0, LED1.green_anode
