# Fritzing sketch infrared_proximity (saved by Fritzing 0.9.2b)
breadboards: 1

parts:
  part = Infrared Proximity Sensor
  part_2 = Arduino Uno (Rev3)

nets:
  N1: part.Vout, part_2.A0
  GND: part.GND, part_2.GND
  VCC: part.Vcc, part_2.5V
