# Fritzing sketch プルダウン回路図 (saved by Fritzing 0.8.7b)
breadboards: 1

parts:
  arduino = Arduino Uno (Rev3)
  S1 = Pushbutton [package="[THT]"]
  R1 = Resistor [tolerance=±5% resistance=10k package=THT]

nets:
  N1: arduino.GND, R1.Pin_1
  N2: arduino.D6_PWM, S1.Pin_3, R1.Pin_0
  N3: arduino.5V, S1.Pin_1, S1.Pin_2
