# Fritzing sketch LEDのフェードインとフェードアウト (saved by Fritzing 0.9.2b)
breadboards: 1

parts:
  aruduino = Arduino Uno (Rev3)
  R1 = Resistor [tolerance=±5% resistance=330 package=THT]
  LED1 = LED - 5mm [color="Red (633nm)" package="5 mm [THT]"]

nets:
  N1: aruduino.D9_PWM, LED1.anode
  N2: aruduino.GND, R1.Pin_0
  N3: R1.Pin_1, LED1.cathode
