# Fritzing sketch 光センサ (saved by Fritzing 0.9.2b)
breadboards: 1

parts:
  arduino = Arduino Uno (Rev3)
  R1 = Photocell (LDR) [package=THT]
  R2 = Resistor [tolerance=±5% resistance=10k package=THT]

nets:
  N1: arduino.A0, R1.pin_0, R2.Pin_1
  N2: arduino.5V, R1.pin_1
  N3: arduino.GND, R2.Pin_0
